# Fritzing sketch Circuit_Diagram (saved by Fritzing 0.8.7b)
breadboards: 1

parts:
  U1 = ESP32S-HiLetgo [part_number=ESP32S-HiLetgo]
  DHT1 = DHT22 Humidity and Temperature Sensor
  o1 = Module display OLED I2C 128x64 SSD1306 [package=THT]
  R1 = Resistor [tolerance=±5% resistance=10k package=THT]

nets:
  N1: U1.3.3, o1.VCC
  GND: U1.GND, DHT1.GND, o1.GND
  VIN: U1.VIN, DHT1.VDD
  N2: U1.GPIO4, R1.Pin_0
  N3: U1.GPIO21, o1.SDA
  N4: U1.GPIO22, o1.SCL
  N5: DHT1.DATA, R1.Pin_1

custom parts:
  ESP32S-HiLetgo: HiLetgo ESP-WROOM-32 ESP32 ESP-32S Development Board 2.4GHz Dual-Mode WiFi + Bluetooth Dual Cores Microcontroller The ESP32 integrated with Antenna switches, RF Balun, power amplifiers, low-noise amplifiers, filters, and management modules, and the entire solution occupies the least area of PCB. 2.4 GHz Wi-Fi plus Bluetooth dual-mode chip, with TSMC Ultra-low power consumption 40nm technology,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
  Module display OLED I2C 128x64 SSD1306: Ecran OLED I2C SSD163 de 128x64 avec connexion I2C
